// Logisim project processor.circ as structural Verilog
module ALU (
  input  [2:0] F___ALUctrl,
  input  [31:0] A,
  input  [31:0] B,
  output [31:0] Y,
  output ZERO
);

  wire [31:0] adder_1_out, and_1_out, bit_extender_1_out, multiplexer_1_out, not_1_out, or_1_out;

  assign not_1_out = ~B;  // NOT_Gate not_1, 32 bits wide
  Multiplexer #(.enable("false"), .width(32)) multiplexer_1 (
    .in0(B), .in1(not_1_out), .out(multiplexer_1_out), .sel(F___ALUctrl[2]));
  Adder #(.width(32)) adder_1 (.a(multiplexer_1_out), .b(A), .out(adder_1_out), .cin(F___ALUctrl[2]));  // open: cout
  assign and_1_out = multiplexer_1_out & A;  // AND_Gate and_1, 32 bits wide
  assign or_1_out = multiplexer_1_out | A;  // OR_Gate or_1, 32 bits wide
  assign bit_extender_1_out = {{31{adder_1_out[31]}}, adder_1_out[31]};  // Bit_Extender bit_extender_1
  Multiplexer #(.enable("false"), .select(2), .width(32)) multiplexer_2 (
    .in0(and_1_out), .in1(or_1_out), .in2(adder_1_out), .in3(bit_extender_1_out), .out(Y),
    .sel(F___ALUctrl[1:0]));
  Comparator #(.mode("unsigned"), .width(32)) comparator_1 (.a(Y), .b({32{1'b0}}), .eq(ZERO));  // open: gt, lt

  // Notes on the sheet:
  //   F 2
  //   A & B
  //   A | B
  //   ADD A B F(2) C_in
  //   zero extension for SLT
  //   F 1:0
  //   if all bits of Y == 0, ZERO is 1
endmodule

module Datapath (
  output [31:0] v0,
  output [31:0] out_2
);

  wire alu_1_zero, and_1_out, clock_1_out, controlunit_1_alusrc, controlunit_1_branch, controlunit_1_regdst,
       controlunit_1_regwrite;
  wire [2:0] bitselector_2_out, bitselector_4_out, bitselector_6_out, controlunit_1_alucontrol,
       multiplexer_2_out;
  wire [6:0] bitselector_1_out;
  wire [7:0] adder_1_out, adder_2_out, bitselector_3_out, bitselector_8_out, multiplexer_1_out, register_1_q,
       shifter_1_out;
  wire [10:0] bitselector_5_out;
  wire [15:0] bitselector_7_out;
  wire [31:0] bit_extender_1_out, multiplexer_3_out, registerfile_1_rd1, registerfile_1_rd2, rom_1_data,
       shifter_2_out;

  Clock clock_1 (.out(clock_1_out));
  Multiplexer #(.enable("false"), .width(8)) multiplexer_1 (
    .in0(adder_1_out), .in1(adder_2_out), .out(multiplexer_1_out), .sel(and_1_out));
  Register register_1 (.D(multiplexer_1_out), .Q(register_1_q), .clk(clock_1_out));  // open: en, clr
  Adder adder_1 (.a(register_1_q), .b(8'h4), .out(adder_1_out));  // open: cin, cout
  Shifter #(.shift("lr")) shifter_1 (.in(register_1_q), .\dist (3'b010), .out(shifter_1_out));
  ROM #(.dataWidth(32)) rom_1 (.addr(shifter_1_out), .data(rom_1_data));
  BitSelector #(.group(7), .width(32)) bitselector_1 (.in(rom_1_data), .out(bitselector_1_out), .sel(3'b011));
  BitSelector #(.group(3), .width(7)) bitselector_2 (.in(bitselector_1_out), .out(bitselector_2_out), .sel(2'b00));
  BitSelector #(.group(8), .width(32)) bitselector_3 (.in(rom_1_data), .out(bitselector_3_out), .sel(2'b10));
  BitSelector #(.group(3)) bitselector_4 (.in(bitselector_3_out), .out(bitselector_4_out), .sel(2'b00));
  BitSelector #(.group(11), .width(32)) bitselector_5 (.in(rom_1_data), .out(bitselector_5_out), .sel(2'b01));
  BitSelector #(.group(3), .width(11)) bitselector_6 (.in(bitselector_5_out), .out(bitselector_6_out), .sel(2'b00));
  BitSelector #(.group(16), .width(32)) bitselector_7 (.in(rom_1_data), .out(bitselector_7_out), .sel(1'b0));
  ControlUnit controlunit_1 (
    .ALUSrc(controlunit_1_alusrc), .RegWrite(controlunit_1_regwrite), .RegDst(controlunit_1_regdst),
    .Branch(controlunit_1_branch), .ALUControl(controlunit_1_alucontrol), .Instruction(rom_1_data));
  RegisterFile registerfile_1 (
    .RD1(registerfile_1_rd1), .RD2(registerfile_1_rd2), .V0(out_2), .WD3(v0), .CLK(clock_1_out),
    .A1(bitselector_2_out), .A2(bitselector_4_out), .A3(multiplexer_2_out), .WE3(controlunit_1_regwrite));
  assign bit_extender_1_out = {{16{bitselector_7_out[15]}}, bitselector_7_out};  // Bit_Extender bit_extender_1
  Multiplexer #(.enable("false"), .width(3)) multiplexer_2 (
    .in0(bitselector_4_out), .in1(bitselector_6_out), .out(multiplexer_2_out), .sel(controlunit_1_regdst));
  Multiplexer #(.enable("false"), .width(32)) multiplexer_3 (
    .in0(registerfile_1_rd2), .in1(bit_extender_1_out), .out(multiplexer_3_out), .sel(controlunit_1_alusrc));
  ALU alu_1 (
    .Y(v0), .ZERO(alu_1_zero), .A(registerfile_1_rd1), .F___ALUctrl(controlunit_1_alucontrol),
    .B(multiplexer_3_out));
  BitSelector #(.group(8), .width(32)) bitselector_8 (.in(shifter_2_out), .out(bitselector_8_out), .sel(2'b00));
  Shifter #(.width(32)) shifter_2 (.in(bit_extender_1_out), .\dist (5'b00010), .out(shifter_2_out));
  and and_1 (and_1_out, controlunit_1_branch, alu_1_zero);
  Adder adder_2 (.a(bitselector_8_out), .b(adder_1_out), .out(adder_2_out));  // open: cin, cout

  // Notes on the sheet:
  //   contents of rom_1 (hex, n*v repeats v):
  //   20040003 20020001 20830001 20060001 10c30009 20c60001 20050000 20070001 10e60003 20e70001 a22820
  //   1000fffc 20a20000 1000fff6 1000ffff
endmodule

module Tests (
  output [31:0] Y,
  output [7:0] out_2,
  output [7:0] out_3,
  output [2:0] out_4
);

  BitSelector #(.group(8), .width(32)) bitselector_1 (.in(32'h12356789), .out(out_2), .sel(2'b01));
  BitSelector #(.group(8), .width(32)) bitselector_2 (.in(32'h12356789), .out(out_3), .sel(2'b01));
  BitSelector #(.group(3)) bitselector_3 (.in(out_3), .out(out_4), .sel(2'b00));

  assign Y = 32'hf4010207;

  // Notes on the sheet:
  //   binary values in Logisim. Convince yourself how the bits are displayed.
  //   Example 2: The bit selector is configured to have 32  
  //   bit group #1 (starting at index 0) is selected for the output.
  //   That is, the 8 bits 0x67 at bit indices 15..8  are sent to the output.
  //   Example 3: Now, assume that you want to extract 3 bits at   
  //   Example 1: A simple example that illustrates how 32-bit values are displayed as 
  //   input bits and 8 output bits. The parameter constant is 1, which means that   
  //   bit indices 10..8. This can be accoplished by putting two bit selecotrs in series.
endmodule

module RegisterFile (
  input  CLK,
  input  [2:0] A1,
  input  [31:0] WD3,
  input  [2:0] A2,
  input  WE3,
  input  [2:0] A3,
  output [31:0] RD1,
  output [31:0] RD2,
  output [31:0] V0
);

  wire and_1_out, and_2_out, and_3_out, and_4_out, and_5_out, and_6_out, and_7_out, and_8_out,
       decoder_1_out0, decoder_1_out1, decoder_1_out2, decoder_1_out3, decoder_1_out4, decoder_1_out5,
       decoder_1_out6, decoder_1_out7;
  wire [31:0] reg__0_q, register_1_q, register_2_q, register_3_q, register_4_q, register_5_q, register_6_q;

  Decoder #(.select(3)) decoder_1 (
    .out0(decoder_1_out0), .out1(decoder_1_out1), .out2(decoder_1_out2), .out3(decoder_1_out3),
    .out4(decoder_1_out4), .out5(decoder_1_out5), .out6(decoder_1_out6), .out7(decoder_1_out7), .sel(A3));  // open: en
  and and_1 (and_1_out, WE3, decoder_1_out0);
  and and_2 (and_2_out, WE3, decoder_1_out1);
  and and_3 (and_3_out, WE3, decoder_1_out2);
  and and_4 (and_4_out, WE3, decoder_1_out3);
  and and_5 (and_5_out, WE3, decoder_1_out4);
  and and_6 (and_6_out, WE3, decoder_1_out5);
  and and_7 (and_7_out, WE3, decoder_1_out6);
  and and_8 (and_8_out, WE3, decoder_1_out7);
  Register #(.width(32)) reg__0 (.D({32{1'b0}}), .en(and_1_out), .Q(reg__0_q), .clk(CLK));  // open: clr
  Register #(.width(32)) register_1 (.D(WD3), .en(and_2_out), .Q(register_1_q), .clk(CLK));  // open: clr
  Register #(.width(32)) u_v0 (.D(WD3), .en(and_3_out), .Q(V0), .clk(CLK));  // open: clr
  Register #(.width(32)) register_2 (.D(WD3), .en(and_4_out), .Q(register_2_q), .clk(CLK));  // open: clr
  Register #(.width(32)) register_3 (.D(WD3), .en(and_5_out), .Q(register_3_q), .clk(CLK));  // open: clr
  Register #(.width(32)) register_4 (.D(WD3), .en(and_6_out), .Q(register_4_q), .clk(CLK));  // open: clr
  Register #(.width(32)) register_5 (.D(WD3), .en(and_7_out), .Q(register_5_q), .clk(CLK));  // open: clr
  Register #(.width(32)) register_6 (.D(WD3), .en(and_8_out), .Q(register_6_q), .clk(CLK));  // open: clr
  Multiplexer #(.select(3), .width(32)) multiplexer_1 (
    .in0(reg__0_q), .in1(register_1_q), .in2(V0), .in3(register_2_q), .in4(register_3_q), .in5(register_4_q),
    .in6(register_5_q), .in7(register_6_q), .out(RD1), .sel(A1));  // open: en
  Multiplexer #(.select(3), .width(32)) multiplexer_2 (
    .in0(reg__0_q), .in1(register_1_q), .in2(V0), .in3(register_2_q), .in4(register_3_q), .in5(register_4_q),
    .in6(register_5_q), .in7(register_6_q), .out(RD2), .sel(A2));  // open: en
endmodule

module ControlUnit (
  input  [31:0] Instruction,
  output ALUSrc,
  output RegWrite,
  output RegDst,
  output Branch,
  output [2:0] ALUControl
);

  wire [5:0] bitselector_1_out;
  wire [31:0] shifter_1_out;

  Shifter #(.shift("lr"), .width(32)) shifter_1 (.in(Instruction), .\dist (5'b11010), .out(shifter_1_out));
  BitSelector #(.group(6), .width(32)) bitselector_1 (.in(shifter_1_out), .out(bitselector_1_out), .sel(3'b000));
  Comparator #(.mode("unsigned"), .width(6)) comparator_1 (
    .a(bitselector_1_out), .b(6'b001000), .eq(ALUSrc));  // open: gt, lt
  Comparator #(.mode("unsigned"), .width(6)) comparator_2 (
    .a(bitselector_1_out), .b({6{1'b0}}), .eq(RegDst));  // open: gt, lt
  Comparator #(.mode("unsigned"), .width(6)) comparator_3 (
    .a(bitselector_1_out), .b(6'b000100), .eq(Branch));  // open: gt, lt
  or or_1 (RegWrite, ALUSrc, RegDst);
  Multiplexer #(.enable("false"), .width(3)) multiplexer_1 (.in0(3'b010), .in1(3'b110), .out(ALUControl), .sel(Branch));

  // Notes on the sheet:
  //   we assume that we can only do add if zero???
  //   and not another R-type function since no funct
  //   lie about having a multiply available for later
  //   shift input 26 steps right
  //   SEL(6,0) -> send out group 0, the OPCODE 
  //   if opcode == 8, addi
  //   if opcode == 0, add
  //   mux with 3 / (2,6) can be disregarded unless opcode is 28, then we'll select 3 as ALUctrl code
  //   if input == 000100, then branch
  //   if opcode == 0,or opcode == 1000, need to write to reg
  //   or when we "multiply"
  //   dont need to set the destination for add immediate
endmodule
