// Logisim project processor-surp.circ as structural Verilog: 6 circuits, main circuit main
module main (
);

  ALU alu_1 ();  // open: Y, zaro, out_5, A, F, B
endmodule

module ALU (
  input  [31:0] A,
  input  [31:0] B,
  input  [2:0] F,
  output [31:0] Y,
  output out_5,
  output zaro
);

  wire [31:0] adder_1_out, and_1_out, bit_extender_1_out, multiplexer_1_out, multiplexer_2_out,
       multiplier_1_out, not_1_out, or_1_out;

  Multiplexer #(.enable("false"), .width(32)) multiplexer_1 (
    .in0(B), .in1(not_1_out), .out(multiplexer_1_out), .sel(F[2]));
  assign not_1_out = ~B;  // NOT_Gate not_1, 32 bits wide
  assign and_1_out = A & multiplexer_1_out;  // AND_Gate and_1, 32 bits wide
  assign or_1_out = A | multiplexer_1_out;  // OR_Gate or_1, 32 bits wide
  Adder #(.width(32)) adder_1 (.a(multiplexer_1_out), .b(A), .out(adder_1_out), .cin(F[2]), .cout(out_5));
  Multiplier #(.width(32)) multiplier_1 (.a(A), .b(multiplexer_1_out), .out(multiplier_1_out));  // open: cin, cout
  assign bit_extender_1_out = {{31{adder_1_out[31]}}, adder_1_out[31]};  // Bit_Extender bit_extender_1
  Multiplexer #(.enable("false"), .width(32)) multiplexer_2 (
    .in0(multiplier_1_out), .in1(bit_extender_1_out), .out(multiplexer_2_out), .sel(F[2]));
  Multiplexer #(.enable("false"), .select(2), .width(32)) multiplexer_3 (
    .in0(and_1_out), .in1(or_1_out), .in2(adder_1_out), .in3(multiplexer_2_out), .out(Y), .sel(F[1:0]));
  Comparator #(.mode("unsigned"), .width(32)) comparator_1 (.a(Y), .b({32{1'b0}}), .eq(zaro));  // open: gt, lt

  // Notes on the sheet:
  //   msb
  //   lsb
  //   msb
  //   lsb
endmodule

module Datapath (
  output [7:0] out_1,
  output [2:0] out_2,
  output [31:0] out_3,
  output [31:0] v0,
  output [31:0] out_5
);

  wire alu_1_zaro, and_1_out, clock_1_out, controlunit_1_alusrc, controlunit_1_branch, controlunit_1_regdst,
       controlunit_1_regwrite;
  wire [2:0] bitselector_4_out, bitselector_5_out, bitselector_6_out, multiplexer_2_out;
  wire [6:0] bitselector_1_out;
  wire [7:0] adder_1_out, adder_2_out, bitselector_2_out, bitselector_8_out, register_1_q, shifter_1_out;
  wire [10:0] bitselector_3_out;
  wire [15:0] bitselector_7_out;
  wire [31:0] bit_extender_1_out, registerfile_1_rd1, registerfile_1_rd2, rom_1_data, shifter_2_out;

  Clock clock_1 (.out(clock_1_out));
  Multiplexer #(.enable("false"), .width(8)) multiplexer_1 (
    .in0(adder_1_out), .in1(adder_2_out), .out(out_1), .sel(and_1_out));
  Register register_1 (.D(out_1), .Q(register_1_q), .clk(clock_1_out));  // open: en, clr
  Shifter #(.shift("lr")) shifter_1 (.in(register_1_q), .\dist (3'b010), .out(shifter_1_out));
  Adder adder_1 (.a(register_1_q), .b(8'h4), .out(adder_1_out));  // open: cin, cout
  ROM #(.dataWidth(32)) rom_1 (.addr(shifter_1_out), .data(rom_1_data));
  BitSelector #(.group(7), .width(32)) bitselector_1 (.in(rom_1_data), .out(bitselector_1_out), .sel(3'b011));
  BitSelector #(.group(8), .width(32)) bitselector_2 (.in(rom_1_data), .out(bitselector_2_out), .sel(2'b10));
  BitSelector #(.group(11), .width(32)) bitselector_3 (.in(rom_1_data), .out(bitselector_3_out), .sel(2'b01));
  BitSelector #(.group(3), .width(7)) bitselector_4 (.in(bitselector_1_out), .out(bitselector_4_out), .sel(2'b00));
  BitSelector #(.group(3)) bitselector_5 (.in(bitselector_2_out), .out(bitselector_5_out), .sel(2'b00));
  BitSelector #(.group(3), .width(11)) bitselector_6 (.in(bitselector_3_out), .out(bitselector_6_out), .sel(2'b00));
  BitSelector #(.group(16), .width(32)) bitselector_7 (.in(rom_1_data), .out(bitselector_7_out), .sel(1'b0));
  ControlUnit controlunit_1 (
    .RegDst(controlunit_1_regdst), .ALUControl(out_2), .ALUSrc(controlunit_1_alusrc),
    .Branch(controlunit_1_branch), .RegWrite(controlunit_1_regwrite), .Instruction(rom_1_data));
  assign bit_extender_1_out = {{16{bitselector_7_out[15]}}, bitselector_7_out};  // Bit_Extender bit_extender_1
  RegisterFile registerfile_1 (
    .RD1(registerfile_1_rd1), .RD2(registerfile_1_rd2), .V0(v0), .WD3(out_3), .CLK(clock_1_out),
    .A1(bitselector_4_out), .A2(bitselector_5_out), .A3(multiplexer_2_out), .WE3(controlunit_1_regwrite));
  Multiplexer #(.enable("false"), .width(3)) multiplexer_2 (
    .in0(bitselector_5_out), .in1(bitselector_6_out), .out(multiplexer_2_out), .sel(controlunit_1_regdst));
  Multiplexer #(.enable("false"), .width(32)) multiplexer_3 (
    .in0(registerfile_1_rd2), .in1(bit_extender_1_out), .out(out_5), .sel(controlunit_1_alusrc));
  BitSelector #(.group(8), .width(32)) bitselector_8 (.in(shifter_2_out), .out(bitselector_8_out), .sel(2'b00));
  Shifter #(.width(32)) shifter_2 (.in(bit_extender_1_out), .\dist (5'b00010), .out(shifter_2_out));
  ALU alu_1 (.Y(out_3), .zaro(alu_1_zaro), .A(registerfile_1_rd1), .F(out_2), .B(out_5));  // open: out_5
  Adder adder_2 (.a(bitselector_8_out), .b(adder_1_out), .out(adder_2_out));  // open: cin, cout
  and and_1 (and_1_out, controlunit_1_branch, alu_1_zaro);

  // Notes on the sheet:
  //   contents of rom_1 (hex, n*v repeats v):
  //   20040003 20050000 20020001 10850003 20a50001 70451002 1000fffc 1000ffff
endmodule

module Tests (
  output [31:0] Y,
  output [7:0] out_2,
  output [7:0] out_3,
  output [2:0] out_4
);

  BitSelector #(.group(8), .width(32)) bitselector_1 (.in(32'h12356789), .out(out_2), .sel(2'b01));
  BitSelector #(.group(8), .width(32)) bitselector_2 (.in(32'h12356789), .out(out_3), .sel(2'b01));
  BitSelector #(.group(3)) bitselector_3 (.in(out_3), .out(out_4), .sel(2'b00));

  assign Y = 32'hf4010207;

  // Notes on the sheet:
  //   binary values in Logisim. Convince yourself how the bits are displayed.
  //   Example 2: The bit selector is configured to have 32  
  //   bit group #1 (starting at index 0) is selected for the output.
  //   That is, the 8 bits 0x67 at bit indices 15..8  are sent to the output.
  //   Example 3: Now, assume that you want to extract 3 bits at   
  //   Example 1: A simple example that illustrates how 32-bit values are displayed as 
  //   input bits and 8 output bits. The parameter constant is 1, which means that   
  //   bit indices 10..8. This can be accoplished by putting two bit selecotrs in series.
endmodule

module RegisterFile (
  input  CLK,
  input  [2:0] A1,
  input  [31:0] WD3,
  input  [2:0] A2,
  input  WE3,
  input  [2:0] A3,
  output [31:0] RD1,
  output [31:0] RD2,
  output [31:0] V0
);

  wire and_1_out, and_2_out, and_3_out, and_4_out, and_5_out, and_6_out, and_7_out, and_8_out,
       decoder_1_out0, decoder_1_out1, decoder_1_out2, decoder_1_out3, decoder_1_out4, decoder_1_out5,
       decoder_1_out6, decoder_1_out7;
  wire [31:0] register_1_q, register_2_q, register_4_q, register_5_q, register_6_q, register_7_q,
       register_8_q;

  Decoder #(.select(3)) decoder_1 (
    .out0(decoder_1_out0), .out1(decoder_1_out1), .out2(decoder_1_out2), .out3(decoder_1_out3),
    .out4(decoder_1_out4), .out5(decoder_1_out5), .out6(decoder_1_out6), .out7(decoder_1_out7), .sel(A3));  // open: en
  and and_1 (and_1_out, WE3, decoder_1_out0);
  and and_2 (and_2_out, WE3, decoder_1_out1);
  and and_3 (and_3_out, WE3, decoder_1_out2);
  and and_4 (and_4_out, WE3, decoder_1_out3);
  and and_5 (and_5_out, WE3, decoder_1_out4);
  and and_6 (and_6_out, WE3, decoder_1_out5);
  and and_7 (and_7_out, WE3, decoder_1_out6);
  and and_8 (and_8_out, WE3, decoder_1_out7);
  Register #(.width(32)) register_1 (.D({32{1'b0}}), .en(and_1_out), .Q(register_1_q));  // open: clk, clr
  Register #(.width(32)) register_2 (.D(WD3), .en(and_2_out), .Q(register_2_q), .clk(CLK));  // open: clr
  Register #(.width(32)) register_3 (.D(WD3), .en(and_3_out), .Q(V0), .clk(CLK));  // open: clr
  Register #(.width(32)) register_4 (.D(WD3), .en(and_4_out), .Q(register_4_q), .clk(CLK));  // open: clr
  Register #(.width(32)) register_5 (.D(WD3), .en(and_5_out), .Q(register_5_q), .clk(CLK));  // open: clr
  Register #(.width(32)) register_6 (.D(WD3), .en(and_6_out), .Q(register_6_q), .clk(CLK));  // open: clr
  Register #(.width(32)) register_7 (.D(WD3), .en(and_7_out), .Q(register_7_q), .clk(CLK));  // open: clr
  Register #(.width(32)) register_8 (.D(WD3), .en(and_8_out), .Q(register_8_q), .clk(CLK));  // open: clr
  Multiplexer #(.select(3), .width(32)) multiplexer_1 (
    .in0(register_1_q), .in1(register_2_q), .in2(V0), .in3(register_4_q), .in4(register_5_q),
    .in5(register_6_q), .in6(register_7_q), .in7(register_8_q), .out(RD1), .sel(A1));  // open: en
  Multiplexer #(.select(3), .width(32)) multiplexer_2 (
    .in0(register_1_q), .in1(register_2_q), .in2(V0), .in3(register_4_q), .in4(register_5_q),
    .in5(register_6_q), .in6(register_7_q), .in7(register_8_q), .out(RD2), .sel(A2));  // open: en
endmodule

module ControlUnit (
  input  [31:0] Instruction,
  output RegDst,
  output RegWrite,
  output ALUSrc,
  output [2:0] ALUControl,
  output Branch
);

  wire comparator_2_eq, comparator_3_eq;
  wire [2:0] multiplexer_1_out;
  wire [5:0] bitselector_1_out;
  wire [31:0] shifter_1_out;

  Shifter #(.shift("lr"), .width(32)) shifter_1 (.in(Instruction), .\dist (5'b11010), .out(shifter_1_out));
  BitSelector #(.group(6), .width(32)) bitselector_1 (.in(shifter_1_out), .out(bitselector_1_out), .sel(3'b000));
  Comparator #(.mode("unsigned"), .width(6)) comparator_1 (
    .a(bitselector_1_out), .b(6'b001000), .eq(ALUSrc));  // open: gt, lt
  Comparator #(.mode("unsigned"), .width(6)) comparator_2 (
    .a(bitselector_1_out), .b({6{1'b0}}), .eq(comparator_2_eq));  // open: gt, lt
  Comparator #(.mode("unsigned"), .width(6)) comparator_3 (
    .a(bitselector_1_out), .b(6'b011100), .eq(comparator_3_eq));  // open: gt, lt
  Comparator #(.mode("unsigned"), .width(6)) comparator_4 (
    .a(bitselector_1_out), .b(6'b000100), .eq(Branch));  // open: gt, lt
  Multiplexer #(.enable("false"), .width(3)) multiplexer_1 (
    .in0(3'b010), .in1(3'b110), .out(multiplexer_1_out), .sel(Branch));
  or or_1 (RegWrite, ALUSrc, comparator_3_eq, comparator_2_eq);
  or or_2 (RegDst, comparator_3_eq, comparator_2_eq);
  Multiplexer #(.enable("false"), .width(3)) multiplexer_2 (
    .in0(multiplexer_1_out), .in1(3'b011), .out(ALUControl), .sel(comparator_3_eq));

  // Notes on the sheet:
  //   Shift input (32bitar) 26 steps right
  //   If opcode == 8, addi
  //   If opcode == 0, add
  //   if opcode == 1c, mul
  //   If opcode == 4, beq
endmodule
